// Logisim project game_of_life.circ as structural Verilog: 1 circuit, main circuit main
module main (
  input  in_1,
  input  N1,
  input  N2,
  input  N3,
  input  N4,
  input  N5,
  input  N6,
  input  N7,
  input  N8,
  output out_10,
  output out_11
);

  wire and_1_out, comparator_1_eq, register_1_q;
  wire [3:0] bitadder_1_out;

  Register #(.width(1)) register_1 (.D(in_1), .Q(register_1_q));  // open: en, clk, clr
  BitAdder bitadder_1 (.in0({N8, N7, N6, N5, N4, N3, N2, N1}), .out(bitadder_1_out));
  Comparator #(.width(4)) comparator_1 (.a(bitadder_1_out), .b(4'b0010), .eq(comparator_1_eq));  // open: gt, lt
  Comparator #(.width(4)) comparator_2 (.a(bitadder_1_out), .b(4'b0011), .eq(out_10));  // open: gt, lt
  and and_1 (and_1_out, register_1_q, comparator_1_eq);
  or or_1 (out_11, and_1_out, out_10);

  // Other names for the same wires on the sheet: birth = out_10; next_state = out_11
endmodule
